// Logisim project tpu.circ as structural Verilog: 5 circuits, main circuit MatMult
module MatMult (
  input  [15:0] in_1,
  input  [15:0] in_2,
  input  [15:0] in_3,
  input  [15:0] in_4,
  input  [15:0] in_5,
  input  [15:0] in_6,
  input  [15:0] in_7,
  input  [15:0] in_8,
  output [15:0] out_9
);

  wire [15:0] adder_1_out, adder_2_out, multiplier_1_out, multiplier_2_out, multiplier_3_out,
       multiplier_4_out;

  Multiplier #(.width(16)) multiplier_1 (.a(in_1), .b(in_2), .out(multiplier_1_out));  // open: cin, cout
  Multiplier #(.width(16)) multiplier_2 (.a(in_3), .b(in_4), .out(multiplier_2_out));  // open: cin, cout
  Multiplier #(.width(16)) multiplier_3 (.a(in_5), .b(in_6), .out(multiplier_3_out));  // open: cin, cout
  Multiplier #(.width(16)) multiplier_4 (.a(in_7), .b(in_8), .out(multiplier_4_out));  // open: cin, cout
  Adder #(.width(16)) adder_1 (.a(multiplier_1_out), .b(multiplier_2_out), .out(adder_1_out));  // open: cin, cout
  Adder #(.width(16)) adder_2 (.a(multiplier_3_out), .b(multiplier_4_out), .out(adder_2_out));  // open: cin, cout
  Adder #(.width(16)) adder_3 (.a(adder_1_out), .b(adder_2_out), .out(out_9));  // open: cin, cout
endmodule

module RCwINST1 (
  input  in_1,
  input  in_2,
  input  in_3
);

  wire and_1_out, and_2_out, and_3_out, and_4_out, and_5_out, and_6_out, and_7_out, and_8_out, and_9_out,
       and_10_out, and_11_out, and_12_out, and_13_out, and_14_out, and_15_out, and_16_out, clock_1_out,
       comparator_1_eq, comparator_2_eq, comparator_3_eq, comparator_4_eq, comparator_5_eq, counter_2_q,
       counter_5_q, counter_8_q, or_1_out, or_2_out, or_3_out, or_4_out, or_5_out, or_6_out, or_7_out,
       or_8_out, register_1_q, register_2_q, register_6_q, undriven, undriven_2, xor_1_out;
  wire [3:0] counter_3_q, counter_4_q, counter_6_q, multiplier_1_out, register_4_q, subtractor_1_out;
  wire [7:0] counter_1_q, counter_7_q, counter_9_q, counter_10_q;
  wire [7:4] register_5_q;
  wire [15:0] controlled_buffer_1_out, controlled_buffer_5_out, controlled_buffer_9_out,
       controlled_buffer_13_out, controlled_buffer_17_out, controlled_buffer_21_out,
       controlled_buffer_25_out, controlled_buffer_29_out, controlled_buffer_33_out, matmult_1_out_9,
       ram_1_dout, ram_2_dout, ram_3_dout, register_3_q, register_7_q, register_8_q, register_9_q,
       register_10_q, register_11_q, register_12_q, register_13_q, register_14_q, register_15_q,
       register_16_q, register_17_q, register_18_q, register_19_q, register_20_q, register_21_q,
       register_22_q, register_23_q, register_24_q, register_25_q, register_26_q, register_27_q,
       register_28_q, register_29_q, register_30_q, register_31_q, register_32_q, register_33_q,
       register_34_q, register_35_q, register_36_q, register_37_q, register_38_q, register_39_q,
       register_40_q, register_41_q, register_42_q, register_43_q, register_44_q, register_45_q,
       register_46_q, register_47_q, register_48_q, register_49_q, register_50_q, register_51_q,
       register_52_q, register_53_q, register_54_q;
  wire [63:0] rom_1_data;

  xor xor_1 (xor_1_out, rom_1_data[0], comparator_2_eq);
  Clock clock_1 (.out(clock_1_out));
  Register #(.width(1)) register_1 (
    .D(or_1_out), .en(or_1_out), .clk(clock_1_out), .Q(register_1_q), .clr(register_1_q));
  or or_1 (or_1_out, xor_1_out, rom_1_data[2]);
  Counter counter_1 (.count(or_2_out), .Q(counter_1_q), .clk(clock_1_out));  // open: load, D, carry, up, clr
  or or_2 (or_2_out, comparator_1_eq, rom_1_data[1]);
  Comparator #(.width(1)) comparator_1 (.a(in_3), .b(counter_2_q), .eq(comparator_1_eq));  // open: gt, lt
  Counter #(.max('h1), .width(1)) counter_2 (
    .load(rom_1_data[0]), .D(rom_1_data[0]), .count(rom_1_data[0]), .Q(counter_2_q), .clk(clock_1_out));  // open: carry, up, clr
  // Probe on counter_3_q
  // Probe on register_5_q
  Counter #(.max('hf), .width(4)) counter_3 (
    .Q(counter_3_q), .clk(clock_1_out), .clr(register_1_q));  // open: load, D, count, carry, up
  RAM #(.dataWidth(16), .\type ("nonvolatile")) ram_1 (
    .addr(counter_1_q), .oe(or_2_out), .clk(clock_1_out), .dout(ram_1_dout));  // open: we, din
  Comparator #(.width(4)) comparator_2 (.a(counter_4_q), .b(counter_3_q), .eq(comparator_2_eq));  // open: gt, lt
  Register #(.width(1)) register_2 (
    .D(undriven), .en(undriven), .clk(undriven_2), .Q(register_2_q), .clr(register_2_q));
  ROM #(.dataWidth(64)) rom_1 (.addr({register_5_q, counter_3_q}), .data(rom_1_data));
  // Probe on ram_1_dout
  Register #(.width(16)) register_3 (
    .D(ram_1_dout), .en(rom_1_data[1]), .clk(clock_1_out), .Q(register_3_q));  // open: clr
  Multiplier #(.width(4)) multiplier_1 (.a(register_4_q), .b(4'b0100), .out(multiplier_1_out));  // open: cin, cout
  Subtractor #(.width(4)) subtractor_1 (.a(multiplier_1_out), .b(4'b0001), .out(subtractor_1_out));  // open: bin, bout
  Counter #(.max('hf), .width(4)) counter_4 (
    .load(1'b1), .D(subtractor_1_out), .Q(counter_4_q), .clk(clock_1_out), .clr(register_6_q));  // open: count, carry, up
  or or_3 (or_3_out, xor_1_out, rom_1_data[3]);
  Register #(.width(4)) register_4 (
    .D(register_3_q[3:0]), .en(rom_1_data[5]), .clk(clock_1_out), .Q(register_4_q), .clr(register_6_q));
  Register #(.width(4)) register_5 (
    .D(register_3_q[15:12]), .en(rom_1_data[7]), .clk(clock_1_out), .Q(register_5_q), .clr(register_6_q));
  Register #(.width(1)) register_6 (
    .D(or_3_out), .en(or_3_out), .clk(clock_1_out), .Q(register_6_q), .clr(register_6_q));
  Counter #(.max('h1), .width(1)) counter_5 (
    .load(rom_1_data[0]), .D(rom_1_data[0]), .count(rom_1_data[0]), .Q(counter_5_q), .clk(clock_1_out));  // open: carry, up, clr
  Comparator #(.width(1)) comparator_3 (.a(in_2), .b(counter_5_q), .eq(comparator_3_eq));  // open: gt, lt
  Comparator #(.width(4)) comparator_4 (.a(4'b0101), .b(counter_6_q), .eq(comparator_4_eq));  // open: gt, lt
  Counter #(.max('hf), .width(4)) counter_6 (
    .Q(counter_6_q), .clk(rom_1_data[4]), .clr(comparator_4_eq));  // open: load, D, count, carry, up
  or or_4 (or_4_out, comparator_3_eq, or_5_out);
  Counter counter_7 (
    .load(rom_1_data[6]), .D(register_3_q[11:4]), .count(or_4_out), .Q(counter_7_q), .clk(clock_1_out),
    .clr(register_6_q));  // open: carry, up
  or or_5 (or_5_out, rom_1_data[23], rom_1_data[22], rom_1_data[21], rom_1_data[20], rom_1_data[19], rom_1_data[18], rom_1_data[17], rom_1_data[16], rom_1_data[15], rom_1_data[14], rom_1_data[13], rom_1_data[12], rom_1_data[11], rom_1_data[10], rom_1_data[9], rom_1_data[8]);
  RAM #(.dataWidth(16), .\type ("nonvolatile")) ram_2 (
    .addr(counter_7_q), .oe(or_4_out), .clk(clock_1_out), .dout(ram_2_dout));  // open: we, din
  Register #(.width(16)) register_7 (
    .D(ram_2_dout), .en(rom_1_data[8]), .clk(clock_1_out), .Q(register_7_q), .clr(comparator_4_eq));
  Register #(.width(16)) register_8 (
    .D(ram_2_dout), .en(rom_1_data[9]), .clk(clock_1_out), .Q(register_8_q), .clr(comparator_4_eq));
  Register #(.width(16)) register_9 (
    .D(ram_2_dout), .en(rom_1_data[10]), .clk(clock_1_out), .Q(register_9_q), .clr(comparator_4_eq));
  Register #(.width(16)) register_10 (
    .D(ram_2_dout), .en(rom_1_data[11]), .clk(clock_1_out), .Q(register_10_q), .clr(comparator_4_eq));
  Register #(.width(16)) register_11 (
    .D(ram_2_dout), .en(rom_1_data[12]), .clk(clock_1_out), .Q(register_11_q), .clr(comparator_4_eq));
  Register #(.width(16)) register_12 (
    .D(ram_2_dout), .en(rom_1_data[13]), .clk(clock_1_out), .Q(register_12_q), .clr(comparator_4_eq));
  Register #(.width(16)) register_13 (
    .D(ram_2_dout), .en(rom_1_data[14]), .clk(clock_1_out), .Q(register_13_q), .clr(comparator_4_eq));
  Register #(.width(16)) register_14 (
    .D(ram_2_dout), .en(rom_1_data[15]), .clk(clock_1_out), .Q(register_14_q), .clr(comparator_4_eq));
  Register #(.width(16)) register_15 (
    .D(ram_2_dout), .en(rom_1_data[16]), .clk(clock_1_out), .Q(register_15_q), .clr(comparator_4_eq));
  Register #(.width(16)) register_16 (
    .D(ram_2_dout), .en(rom_1_data[17]), .clk(clock_1_out), .Q(register_16_q), .clr(comparator_4_eq));
  Register #(.width(16)) register_17 (
    .D(ram_2_dout), .en(rom_1_data[18]), .clk(clock_1_out), .Q(register_17_q), .clr(comparator_4_eq));
  Register #(.width(16)) register_18 (
    .D(ram_2_dout), .en(rom_1_data[19]), .clk(clock_1_out), .Q(register_18_q), .clr(comparator_4_eq));
  Register #(.width(16)) register_19 (
    .D(ram_2_dout), .en(rom_1_data[20]), .clk(clock_1_out), .Q(register_19_q), .clr(comparator_4_eq));
  Register #(.width(16)) register_20 (
    .D(ram_2_dout), .en(rom_1_data[21]), .clk(clock_1_out), .Q(register_20_q), .clr(comparator_4_eq));
  Register #(.width(16)) register_21 (
    .D(ram_2_dout), .en(rom_1_data[22]), .clk(clock_1_out), .Q(register_21_q), .clr(comparator_4_eq));
  Register #(.width(16)) register_22 (
    .D(ram_2_dout), .en(rom_1_data[23]), .clk(clock_1_out), .Q(register_22_q), .clr(comparator_4_eq));
  assign controlled_buffer_1_out = rom_1_data[40] ? register_7_q : 16'bz;  // Controlled_Buffer controlled_buffer_1
  assign controlled_buffer_1_out = rom_1_data[41] ? register_8_q : 16'bz;  // Controlled_Buffer controlled_buffer_2
  assign controlled_buffer_1_out = rom_1_data[42] ? register_9_q : 16'bz;  // Controlled_Buffer controlled_buffer_3
  assign controlled_buffer_1_out = rom_1_data[43] ? register_10_q : 16'bz;  // Controlled_Buffer controlled_buffer_4
  assign controlled_buffer_5_out = rom_1_data[40] ? register_11_q : 16'bz;  // Controlled_Buffer controlled_buffer_5
  assign controlled_buffer_5_out = rom_1_data[41] ? register_12_q : 16'bz;  // Controlled_Buffer controlled_buffer_6
  assign controlled_buffer_5_out = rom_1_data[42] ? register_13_q : 16'bz;  // Controlled_Buffer controlled_buffer_7
  assign controlled_buffer_5_out = rom_1_data[43] ? register_14_q : 16'bz;  // Controlled_Buffer controlled_buffer_8
  assign controlled_buffer_9_out = rom_1_data[40] ? register_15_q : 16'bz;  // Controlled_Buffer controlled_buffer_9
  assign controlled_buffer_9_out = rom_1_data[41] ? register_16_q : 16'bz;  // Controlled_Buffer controlled_buffer_10
  assign controlled_buffer_9_out = rom_1_data[42] ? register_17_q : 16'bz;  // Controlled_Buffer controlled_buffer_11
  assign controlled_buffer_9_out = rom_1_data[43] ? register_18_q : 16'bz;  // Controlled_Buffer controlled_buffer_12
  assign controlled_buffer_13_out = rom_1_data[40] ? register_19_q : 16'bz;  // Controlled_Buffer controlled_buffer_13
  assign controlled_buffer_13_out = rom_1_data[41] ? register_20_q : 16'bz;  // Controlled_Buffer controlled_buffer_14
  assign controlled_buffer_13_out = rom_1_data[42] ? register_21_q : 16'bz;  // Controlled_Buffer controlled_buffer_15
  assign controlled_buffer_13_out = rom_1_data[43] ? register_22_q : 16'bz;  // Controlled_Buffer controlled_buffer_16
  Counter #(.max('h1), .width(1)) counter_8 (
    .load(rom_1_data[0]), .D(rom_1_data[0]), .count(rom_1_data[0]), .Q(counter_8_q), .clk(clock_1_out));  // open: carry, up, clr
  Comparator #(.width(1)) comparator_5 (.a(in_1), .b(counter_8_q), .eq(comparator_5_eq));  // open: gt, lt
  or or_6 (or_6_out, comparator_5_eq, or_7_out);
  RAM #(.dataWidth(16), .\type ("nonvolatile")) ram_3 (
    .addr(counter_9_q), .oe(or_6_out), .clk(clock_1_out), .dout(ram_3_dout));  // open: we, din
  Counter counter_9 (
    .load(rom_1_data[6]), .D(register_3_q[11:4]), .count(or_6_out), .Q(counter_9_q), .clk(clock_1_out));  // open: carry, up, clr
  or or_7 (or_7_out, rom_1_data[39], rom_1_data[38], rom_1_data[37], rom_1_data[36], rom_1_data[35], rom_1_data[34], rom_1_data[33], rom_1_data[32], rom_1_data[31], rom_1_data[30], rom_1_data[29], rom_1_data[28], rom_1_data[27], rom_1_data[26], rom_1_data[25], rom_1_data[24]);
  Register #(.width(16)) register_23 (
    .D(ram_3_dout), .en(rom_1_data[24]), .clk(clock_1_out), .Q(register_23_q), .clr(comparator_4_eq));
  Register #(.width(16)) register_24 (
    .D(ram_3_dout), .en(rom_1_data[25]), .clk(clock_1_out), .Q(register_24_q), .clr(comparator_4_eq));
  Register #(.width(16)) register_25 (
    .D(ram_3_dout), .en(rom_1_data[26]), .clk(clock_1_out), .Q(register_25_q), .clr(comparator_4_eq));
  Register #(.width(16)) register_26 (
    .D(ram_3_dout), .en(rom_1_data[27]), .clk(clock_1_out), .Q(register_26_q), .clr(comparator_4_eq));
  Register #(.width(16)) register_27 (
    .D(ram_3_dout), .en(rom_1_data[28]), .clk(clock_1_out), .Q(register_27_q), .clr(comparator_4_eq));
  Register #(.width(16)) register_28 (
    .D(ram_3_dout), .en(rom_1_data[29]), .clk(clock_1_out), .Q(register_28_q), .clr(comparator_4_eq));
  Register #(.width(16)) register_29 (
    .D(ram_3_dout), .en(rom_1_data[30]), .clk(clock_1_out), .Q(register_29_q), .clr(comparator_4_eq));
  Register #(.width(16)) register_30 (
    .D(ram_3_dout), .en(rom_1_data[31]), .clk(clock_1_out), .Q(register_30_q), .clr(comparator_4_eq));
  Register #(.width(16)) register_31 (
    .D(ram_3_dout), .en(rom_1_data[32]), .clk(clock_1_out), .Q(register_31_q), .clr(comparator_4_eq));
  Register #(.width(16)) register_32 (
    .D(ram_3_dout), .en(rom_1_data[33]), .clk(clock_1_out), .Q(register_32_q), .clr(comparator_4_eq));
  Register #(.width(16)) register_33 (
    .D(ram_3_dout), .en(rom_1_data[34]), .clk(clock_1_out), .Q(register_33_q), .clr(comparator_4_eq));
  Register #(.width(16)) register_34 (
    .D(ram_3_dout), .en(rom_1_data[35]), .clk(clock_1_out), .Q(register_34_q), .clr(comparator_4_eq));
  Register #(.width(16)) register_35 (
    .D(ram_3_dout), .en(rom_1_data[36]), .clk(clock_1_out), .Q(register_35_q), .clr(comparator_4_eq));
  Register #(.width(16)) register_36 (
    .D(ram_3_dout), .en(rom_1_data[37]), .clk(clock_1_out), .Q(register_36_q), .clr(comparator_4_eq));
  Register #(.width(16)) register_37 (
    .D(ram_3_dout), .en(rom_1_data[38]), .clk(clock_1_out), .Q(register_37_q), .clr(comparator_4_eq));
  Register #(.width(16)) register_38 (
    .D(ram_3_dout), .en(rom_1_data[39]), .clk(clock_1_out), .Q(register_38_q), .clr(comparator_4_eq));
  assign controlled_buffer_17_out = rom_1_data[44] ? register_23_q : 16'bz;  // Controlled_Buffer controlled_buffer_17
  assign controlled_buffer_17_out = rom_1_data[45] ? register_24_q : 16'bz;  // Controlled_Buffer controlled_buffer_18
  assign controlled_buffer_17_out = rom_1_data[46] ? register_25_q : 16'bz;  // Controlled_Buffer controlled_buffer_19
  assign controlled_buffer_17_out = rom_1_data[47] ? register_26_q : 16'bz;  // Controlled_Buffer controlled_buffer_20
  assign controlled_buffer_21_out = rom_1_data[44] ? register_27_q : 16'bz;  // Controlled_Buffer controlled_buffer_21
  assign controlled_buffer_21_out = rom_1_data[45] ? register_28_q : 16'bz;  // Controlled_Buffer controlled_buffer_22
  assign controlled_buffer_21_out = rom_1_data[46] ? register_29_q : 16'bz;  // Controlled_Buffer controlled_buffer_23
  assign controlled_buffer_21_out = rom_1_data[47] ? register_30_q : 16'bz;  // Controlled_Buffer controlled_buffer_24
  assign controlled_buffer_25_out = rom_1_data[44] ? register_31_q : 16'bz;  // Controlled_Buffer controlled_buffer_25
  assign controlled_buffer_25_out = rom_1_data[45] ? register_32_q : 16'bz;  // Controlled_Buffer controlled_buffer_26
  assign controlled_buffer_25_out = rom_1_data[46] ? register_33_q : 16'bz;  // Controlled_Buffer controlled_buffer_27
  assign controlled_buffer_25_out = rom_1_data[47] ? register_34_q : 16'bz;  // Controlled_Buffer controlled_buffer_28
  assign controlled_buffer_29_out = rom_1_data[44] ? register_35_q : 16'bz;  // Controlled_Buffer controlled_buffer_29
  assign controlled_buffer_29_out = rom_1_data[45] ? register_36_q : 16'bz;  // Controlled_Buffer controlled_buffer_30
  assign controlled_buffer_29_out = rom_1_data[46] ? register_37_q : 16'bz;  // Controlled_Buffer controlled_buffer_31
  assign controlled_buffer_29_out = rom_1_data[47] ? register_38_q : 16'bz;  // Controlled_Buffer controlled_buffer_32
  MatMult matmult_1 (
    .in_1(controlled_buffer_1_out), .in_2(controlled_buffer_17_out), .in_3(controlled_buffer_5_out),
    .in_4(controlled_buffer_21_out), .in_5(controlled_buffer_9_out), .in_6(controlled_buffer_25_out),
    .in_7(controlled_buffer_13_out), .in_8(controlled_buffer_29_out), .out_9(matmult_1_out_9));
  and and_1 (and_1_out, rom_1_data[40], rom_1_data[44]);
  and and_2 (and_2_out, rom_1_data[40], rom_1_data[45]);
  and and_3 (and_3_out, rom_1_data[40], rom_1_data[46]);
  and and_4 (and_4_out, rom_1_data[40], rom_1_data[47]);
  and and_5 (and_5_out, rom_1_data[41], rom_1_data[44]);
  and and_6 (and_6_out, rom_1_data[41], rom_1_data[45]);
  and and_7 (and_7_out, rom_1_data[41], rom_1_data[46]);
  and and_8 (and_8_out, rom_1_data[41], rom_1_data[47]);
  and and_9 (and_9_out, rom_1_data[42], rom_1_data[44]);
  and and_10 (and_10_out, rom_1_data[42], rom_1_data[45]);
  and and_11 (and_11_out, rom_1_data[42], rom_1_data[46]);
  and and_12 (and_12_out, rom_1_data[42], rom_1_data[47]);
  and and_13 (and_13_out, rom_1_data[43], rom_1_data[44]);
  and and_14 (and_14_out, rom_1_data[43], rom_1_data[45]);
  and and_15 (and_15_out, rom_1_data[43], rom_1_data[46]);
  and and_16 (and_16_out, rom_1_data[43], rom_1_data[47]);
  Register #(.width(16)) register_39 (
    .D(matmult_1_out_9), .en(and_1_out), .clk(clock_1_out), .Q(register_39_q), .clr(comparator_4_eq));
  Register #(.width(16)) register_40 (
    .D(matmult_1_out_9), .en(and_2_out), .clk(clock_1_out), .Q(register_40_q), .clr(comparator_4_eq));
  Register #(.width(16)) register_41 (
    .D(matmult_1_out_9), .en(and_3_out), .clk(clock_1_out), .Q(register_41_q), .clr(comparator_4_eq));
  Register #(.width(16)) register_42 (
    .D(matmult_1_out_9), .en(and_4_out), .clk(clock_1_out), .Q(register_42_q), .clr(comparator_4_eq));
  Register #(.width(16)) register_43 (
    .D(matmult_1_out_9), .en(and_5_out), .clk(clock_1_out), .Q(register_43_q), .clr(comparator_4_eq));
  Register #(.width(16)) register_44 (
    .D(matmult_1_out_9), .en(and_6_out), .clk(clock_1_out), .Q(register_44_q), .clr(comparator_4_eq));
  Register #(.width(16)) register_45 (
    .D(matmult_1_out_9), .en(and_7_out), .clk(clock_1_out), .Q(register_45_q), .clr(comparator_4_eq));
  Register #(.width(16)) register_46 (
    .D(matmult_1_out_9), .en(and_8_out), .clk(clock_1_out), .Q(register_46_q), .clr(comparator_4_eq));
  Register #(.width(16)) register_47 (
    .D(matmult_1_out_9), .en(and_9_out), .clk(clock_1_out), .Q(register_47_q), .clr(comparator_4_eq));
  Register #(.width(16)) register_48 (
    .D(matmult_1_out_9), .en(and_10_out), .clk(clock_1_out), .Q(register_48_q), .clr(comparator_4_eq));
  Register #(.width(16)) register_49 (
    .D(matmult_1_out_9), .en(and_11_out), .clk(clock_1_out), .Q(register_49_q), .clr(comparator_4_eq));
  Register #(.width(16)) register_50 (
    .D(matmult_1_out_9), .en(and_12_out), .clk(clock_1_out), .Q(register_50_q), .clr(comparator_4_eq));
  Register #(.width(16)) register_51 (
    .D(matmult_1_out_9), .en(and_13_out), .clk(clock_1_out), .Q(register_51_q), .clr(comparator_4_eq));
  Register #(.width(16)) register_52 (
    .D(matmult_1_out_9), .en(and_14_out), .clk(clock_1_out), .Q(register_52_q), .clr(comparator_4_eq));
  Register #(.width(16)) register_53 (
    .D(matmult_1_out_9), .en(and_15_out), .clk(clock_1_out), .Q(register_53_q), .clr(comparator_4_eq));
  Register #(.width(16)) register_54 (
    .D(matmult_1_out_9), .en(and_16_out), .clk(clock_1_out), .Q(register_54_q), .clr(comparator_4_eq));
  assign controlled_buffer_33_out = rom_1_data[48] ? register_39_q : 16'bz;  // Controlled_Buffer controlled_buffer_33
  assign controlled_buffer_33_out = rom_1_data[49] ? register_40_q : 16'bz;  // Controlled_Buffer controlled_buffer_34
  assign controlled_buffer_33_out = rom_1_data[50] ? register_41_q : 16'bz;  // Controlled_Buffer controlled_buffer_35
  assign controlled_buffer_33_out = rom_1_data[51] ? register_42_q : 16'bz;  // Controlled_Buffer controlled_buffer_36
  assign controlled_buffer_33_out = rom_1_data[52] ? register_43_q : 16'bz;  // Controlled_Buffer controlled_buffer_37
  assign controlled_buffer_33_out = rom_1_data[53] ? register_44_q : 16'bz;  // Controlled_Buffer controlled_buffer_38
  assign controlled_buffer_33_out = rom_1_data[54] ? register_45_q : 16'bz;  // Controlled_Buffer controlled_buffer_39
  assign controlled_buffer_33_out = rom_1_data[55] ? register_46_q : 16'bz;  // Controlled_Buffer controlled_buffer_40
  assign controlled_buffer_33_out = rom_1_data[56] ? register_47_q : 16'bz;  // Controlled_Buffer controlled_buffer_41
  assign controlled_buffer_33_out = rom_1_data[57] ? register_48_q : 16'bz;  // Controlled_Buffer controlled_buffer_42
  assign controlled_buffer_33_out = rom_1_data[58] ? register_49_q : 16'bz;  // Controlled_Buffer controlled_buffer_43
  assign controlled_buffer_33_out = rom_1_data[59] ? register_50_q : 16'bz;  // Controlled_Buffer controlled_buffer_44
  assign controlled_buffer_33_out = rom_1_data[60] ? register_51_q : 16'bz;  // Controlled_Buffer controlled_buffer_45
  assign controlled_buffer_33_out = rom_1_data[61] ? register_52_q : 16'bz;  // Controlled_Buffer controlled_buffer_46
  assign controlled_buffer_33_out = rom_1_data[62] ? register_53_q : 16'bz;  // Controlled_Buffer controlled_buffer_47
  assign controlled_buffer_33_out = rom_1_data[63] ? register_54_q : 16'bz;  // Controlled_Buffer controlled_buffer_48
  or or_8 (or_8_out, rom_1_data[48], rom_1_data[49], rom_1_data[50], rom_1_data[51], rom_1_data[52], rom_1_data[53], rom_1_data[54], rom_1_data[55], rom_1_data[56], rom_1_data[57], rom_1_data[58], rom_1_data[59], rom_1_data[60], rom_1_data[61], rom_1_data[62], rom_1_data[63]);
  RAM #(.dataWidth(16)) ram_4 (
    .addr(counter_10_q), .we(or_8_out), .clk(clock_1_out), .din(controlled_buffer_33_out));  // open: oe, dout
  Counter counter_10 (
    .load(rom_1_data[48]), .D(register_3_q[11:4]), .count(or_8_out), .Q(counter_10_q), .clk(clock_1_out));  // open: carry, up, clr

  // Notes on the sheet:
  //   Used OR Gate Bcoz
  //   COMP with dim will
  //    reset PCU
  //   and JMP
  //   statement also req
  //   PCU Reset
  //   1. INST RAM
  //   1. MBR
  //   1. RES ROM Count
  //   2. Flag
  //   2. DIM
  //   2. Add
  //   2. OPC
  //   PC
  //   CYCLE = 1
  //   ROM COUNTER
  //   OPCODE
  //   DECODER
  //   JMP + RESET
  //   RESETS PCU (DOESNT
  //   RESET OPC SIGNAL)
  //   RAM GARBAGE CONTROLLER
  //   ONLY CLEAR GARBAGE WHEN
  //   USED XOR GATE TO NULLIFY FIRST == SIGNAL FROM COMPARATOR
  //   THIS WILL ALSO GET RESET WITH OPC ONCE
  //   DIMENSION = COUNT
  //   DIMENSION SHOULD ONLY BE INCLUDED IN LOAD A AND B
  //   ADDRESS OF FIRST MATRIX SHOULD BE +1 BCOZ OF GARBAGE
  //   ADDRESS SHOULD BE INCLUDED IN LOAD A, B AND STORE C
  //   INSTRUCTION RAM
  //   PULSE GENERATOR
  //   contents of rom_1 (hex, n*v repeats v):
  //   1 2 f4 13*0 100 200 400 800 1000 2000 4000 8000 10000 20000 40000 80000 100000 200000 400000 800008
  //   1000000 2000000 4000000 8000000 10000000 20000000 40000000 80000000 100000000 200000000 400000000
  //   800000000 1000000000 2000000000 4000000000 8000000008 110000000000 120000000000 140000000000
  //   180000000000 210000000000 220000000000 240000000000 280000000000 410000000000 420000000000
  //   440000000000 480000000000 810000000000 820000000000 840000000000 880000000008 1000000000000
  //   2000000000000 4000000000000 8000000000000 10000000000000 20000000000000 40000000000000
  //   80000000000000 100000000000000 200000000000000 400000000000000 800000000000000 1000000000000000
  //   2000000000000000 4000000000000000 8000000000000000 1c
  //   ROM PCU
  //   MBR
  //   RESET SYNC
  //   RESET OPC SIGNAL
  //   THIS WILL ALSO GET RESET WITH OPC ONCE
  //   RESET LINE FOR ALL REGISTER, RESET WHEN OPCC LOADS VALUE 4 TIMES
  //   ADDRESS IS DIRECTLY CONNECTED TO COUNTER WE
  //   ADD PADDING MANUALLY FOR Less < 4x4 Matrices
  //   RESULTANT MATRIX IS TRANSPOSED
endmodule

module TilingCore (
  input  [15:0] A1,
  input  [15:0] A2,
  input  [15:0] A3,
  input  [15:0] A4,
  input  [15:0] B1,
  input  [15:0] B2,
  input  [15:0] B3,
  input  [15:0] B4,
  input  [15:0] A5,
  input  [15:0] A6,
  input  [15:0] A7,
  input  [15:0] A8,
  input  [15:0] B5,
  input  [15:0] B6,
  input  [15:0] B7,
  input  [15:0] B8,
  input  [15:0] A9,
  input  [15:0] A10,
  input  [15:0] A11,
  input  [15:0] A12,
  input  [15:0] B9,
  input  [15:0] B10,
  input  [15:0] B11,
  input  [15:0] B12,
  input  [15:0] A13,
  input  [15:0] A14,
  input  [15:0] A15,
  input  [15:0] A16,
  input  [15:0] B13,
  input  [15:0] B14,
  input  [15:0] B15,
  input  [15:0] B16,
  output [15:0] C1,
  output [15:0] C2,
  output [15:0] C3,
  output [15:0] C4,
  output [15:0] C5,
  output [15:0] C6,
  output [15:0] C7,
  output [15:0] C8,
  output [15:0] C9,
  output [15:0] C10,
  output [15:0] C11,
  output [15:0] C12,
  output [15:0] C13,
  output [15:0] C14,
  output [15:0] C15,
  output [15:0] C16
);

  wire [15:0] adder_1_out, adder_2_out, adder_3_out, adder_4_out, adder_6_out, adder_7_out, adder_9_out,
       adder_10_out, adder_11_out, adder_12_out, adder_13_out, adder_15_out, adder_16_out, adder_17_out,
       adder_18_out, adder_19_out, adder_20_out, adder_21_out, adder_22_out, adder_23_out, adder_25_out,
       adder_26_out, adder_27_out, adder_28_out, adder_29_out, adder_30_out, adder_40_out, adder_41_out,
       adder_42_out, adder_43_out, adder_44_out, adder_45_out, multiplier_1_out, multiplier_2_out,
       multiplier_3_out, multiplier_4_out, multiplier_5_out, multiplier_6_out, multiplier_7_out,
       multiplier_8_out, multiplier_9_out, multiplier_10_out, multiplier_11_out, multiplier_12_out,
       multiplier_13_out, multiplier_14_out, multiplier_15_out, multiplier_16_out, multiplier_17_out,
       multiplier_18_out, multiplier_19_out, multiplier_20_out, multiplier_21_out, multiplier_22_out,
       multiplier_23_out, multiplier_24_out, multiplier_25_out, multiplier_26_out, multiplier_27_out,
       multiplier_28_out, multiplier_29_out, multiplier_30_out, multiplier_31_out, multiplier_32_out,
       multiplier_33_out, multiplier_34_out, multiplier_35_out, multiplier_36_out, multiplier_37_out,
       multiplier_38_out, multiplier_39_out, multiplier_40_out, multiplier_41_out, multiplier_42_out,
       multiplier_43_out, multiplier_44_out, multiplier_45_out, multiplier_46_out, multiplier_47_out,
       multiplier_48_out, multiplier_49_out, multiplier_50_out, multiplier_51_out, multiplier_52_out,
       multiplier_53_out, multiplier_54_out, multiplier_55_out, multiplier_56_out, multiplier_57_out,
       multiplier_58_out, multiplier_59_out, multiplier_60_out, multiplier_61_out, multiplier_62_out,
       multiplier_63_out, multiplier_64_out;

  Multiplier #(.width(16)) multiplier_1 (.a(A3), .b(B7), .out(multiplier_1_out));  // open: cin, cout
  Multiplier #(.width(16)) multiplier_2 (.a(A4), .b(B8), .out(multiplier_2_out));  // open: cin, cout
  Multiplier #(.width(16)) multiplier_3 (.a(A1), .b(B5), .out(multiplier_3_out));  // open: cin, cout
  Multiplier #(.width(16)) multiplier_4 (.a(A2), .b(B6), .out(multiplier_4_out));  // open: cin, cout
  Multiplier #(.width(16)) multiplier_5 (.a(A1), .b(B1), .out(multiplier_5_out));  // open: cin, cout
  Multiplier #(.width(16)) multiplier_6 (.a(A2), .b(B2), .out(multiplier_6_out));  // open: cin, cout
  Multiplier #(.width(16)) multiplier_7 (.a(A3), .b(B3), .out(multiplier_7_out));  // open: cin, cout
  Multiplier #(.width(16)) multiplier_8 (.a(A4), .b(B4), .out(multiplier_8_out));  // open: cin, cout
  Adder #(.width(16)) adder_1 (.a(multiplier_1_out), .b(multiplier_2_out), .out(adder_1_out));  // open: cin, cout
  Multiplier #(.width(16)) multiplier_9 (.a(A1), .b(B9), .out(multiplier_9_out));  // open: cin, cout
  Multiplier #(.width(16)) multiplier_10 (.a(A2), .b(B10), .out(multiplier_10_out));  // open: cin, cout
  Multiplier #(.width(16)) multiplier_11 (.a(A3), .b(B11), .out(multiplier_11_out));  // open: cin, cout
  Multiplier #(.width(16)) multiplier_12 (.a(A4), .b(B12), .out(multiplier_12_out));  // open: cin, cout
  Adder #(.width(16)) adder_2 (.a(multiplier_3_out), .b(multiplier_4_out), .out(adder_2_out));  // open: cin, cout
  Multiplier #(.width(16)) multiplier_13 (.a(A1), .b(B13), .out(multiplier_13_out));  // open: cin, cout
  Multiplier #(.width(16)) multiplier_14 (.a(A2), .b(B14), .out(multiplier_14_out));  // open: cin, cout
  Multiplier #(.width(16)) multiplier_15 (.a(A3), .b(B15), .out(multiplier_15_out));  // open: cin, cout
  Multiplier #(.width(16)) multiplier_16 (.a(A4), .b(B16), .out(multiplier_16_out));  // open: cin, cout
  Multiplier #(.width(16)) multiplier_17 (.a(A15), .b(B3), .out(multiplier_17_out));  // open: cin, cout
  Multiplier #(.width(16)) multiplier_18 (.a(A16), .b(B4), .out(multiplier_18_out));  // open: cin, cout
  Multiplier #(.width(16)) multiplier_19 (.a(A15), .b(B11), .out(multiplier_19_out));  // open: cin, cout
  Multiplier #(.width(16)) multiplier_20 (.a(A16), .b(B12), .out(multiplier_20_out));  // open: cin, cout
  Multiplier #(.width(16)) multiplier_21 (.a(A15), .b(B15), .out(multiplier_21_out));  // open: cin, cout
  Multiplier #(.width(16)) multiplier_22 (.a(A16), .b(B16), .out(multiplier_22_out));  // open: cin, cout
  Adder #(.width(16)) adder_3 (.a(multiplier_5_out), .b(multiplier_6_out), .out(adder_3_out));  // open: cin, cout
  Adder #(.width(16)) adder_4 (.a(multiplier_7_out), .b(multiplier_8_out), .out(adder_4_out));  // open: cin, cout
  Adder #(.width(16)) adder_5 (.a(adder_2_out), .b(adder_1_out), .out(C2));  // open: cin, cout
  Multiplier #(.width(16)) multiplier_23 (.a(A7), .b(B3), .out(multiplier_23_out));  // open: cin, cout
  Multiplier #(.width(16)) multiplier_24 (.a(A8), .b(B4), .out(multiplier_24_out));  // open: cin, cout
  Multiplier #(.width(16)) multiplier_25 (.a(A7), .b(B11), .out(multiplier_25_out));  // open: cin, cout
  Multiplier #(.width(16)) multiplier_26 (.a(A8), .b(B12), .out(multiplier_26_out));  // open: cin, cout
  Multiplier #(.width(16)) multiplier_27 (.a(A7), .b(B15), .out(multiplier_27_out));  // open: cin, cout
  Multiplier #(.width(16)) multiplier_28 (.a(A8), .b(B16), .out(multiplier_28_out));  // open: cin, cout
  Multiplier #(.width(16)) multiplier_29 (.a(A11), .b(B3), .out(multiplier_29_out));  // open: cin, cout
  Multiplier #(.width(16)) multiplier_30 (.a(A12), .b(B4), .out(multiplier_30_out));  // open: cin, cout
  Multiplier #(.width(16)) multiplier_31 (.a(A11), .b(B11), .out(multiplier_31_out));  // open: cin, cout
  Multiplier #(.width(16)) multiplier_32 (.a(A12), .b(B12), .out(multiplier_32_out));  // open: cin, cout
  Multiplier #(.width(16)) multiplier_33 (.a(A11), .b(B15), .out(multiplier_33_out));  // open: cin, cout
  Multiplier #(.width(16)) multiplier_34 (.a(A12), .b(B16), .out(multiplier_34_out));  // open: cin, cout
  Multiplier #(.width(16)) multiplier_35 (.a(A13), .b(B1), .out(multiplier_35_out));  // open: cin, cout
  Multiplier #(.width(16)) multiplier_36 (.a(A14), .b(B2), .out(multiplier_36_out));  // open: cin, cout
  Multiplier #(.width(16)) multiplier_37 (.a(A13), .b(B9), .out(multiplier_37_out));  // open: cin, cout
  Multiplier #(.width(16)) multiplier_38 (.a(A14), .b(B10), .out(multiplier_38_out));  // open: cin, cout
  Multiplier #(.width(16)) multiplier_39 (.a(A13), .b(B13), .out(multiplier_39_out));  // open: cin, cout
  Multiplier #(.width(16)) multiplier_40 (.a(A14), .b(B14), .out(multiplier_40_out));  // open: cin, cout
  Adder #(.width(16)) adder_6 (.a(multiplier_9_out), .b(multiplier_10_out), .out(adder_6_out));  // open: cin, cout
  Adder #(.width(16)) adder_7 (.a(multiplier_11_out), .b(multiplier_12_out), .out(adder_7_out));  // open: cin, cout
  Multiplier #(.width(16)) multiplier_41 (.a(A5), .b(B1), .out(multiplier_41_out));  // open: cin, cout
  Multiplier #(.width(16)) multiplier_42 (.a(A6), .b(B2), .out(multiplier_42_out));  // open: cin, cout
  Multiplier #(.width(16)) multiplier_43 (.a(A5), .b(B9), .out(multiplier_43_out));  // open: cin, cout
  Multiplier #(.width(16)) multiplier_44 (.a(A6), .b(B10), .out(multiplier_44_out));  // open: cin, cout
  Multiplier #(.width(16)) multiplier_45 (.a(A5), .b(B13), .out(multiplier_45_out));  // open: cin, cout
  Multiplier #(.width(16)) multiplier_46 (.a(A6), .b(B14), .out(multiplier_46_out));  // open: cin, cout
  Multiplier #(.width(16)) multiplier_47 (.a(A9), .b(B1), .out(multiplier_47_out));  // open: cin, cout
  Multiplier #(.width(16)) multiplier_48 (.a(A10), .b(B2), .out(multiplier_48_out));  // open: cin, cout
  Multiplier #(.width(16)) multiplier_49 (.a(A9), .b(B9), .out(multiplier_49_out));  // open: cin, cout
  Multiplier #(.width(16)) multiplier_50 (.a(A10), .b(B10), .out(multiplier_50_out));  // open: cin, cout
  Multiplier #(.width(16)) multiplier_51 (.a(A9), .b(B13), .out(multiplier_51_out));  // open: cin, cout
  Multiplier #(.width(16)) multiplier_52 (.a(A10), .b(B14), .out(multiplier_52_out));  // open: cin, cout
  Adder #(.width(16)) adder_8 (.a(adder_3_out), .b(adder_4_out), .out(C1));  // open: cin, cout
  Adder #(.width(16)) adder_9 (.a(multiplier_13_out), .b(multiplier_14_out), .out(adder_9_out));  // open: cin, cout
  Adder #(.width(16)) adder_10 (.a(multiplier_15_out), .b(multiplier_16_out), .out(adder_10_out));  // open: cin, cout
  Adder #(.width(16)) adder_11 (.a(multiplier_17_out), .b(multiplier_18_out), .out(adder_11_out));  // open: cin, cout
  Adder #(.width(16)) adder_12 (.a(multiplier_19_out), .b(multiplier_20_out), .out(adder_12_out));  // open: cin, cout
  Adder #(.width(16)) adder_13 (.a(multiplier_21_out), .b(multiplier_22_out), .out(adder_13_out));  // open: cin, cout
  Adder #(.width(16)) adder_14 (.a(adder_6_out), .b(adder_7_out), .out(C3));  // open: cin, cout
  Adder #(.width(16)) adder_15 (.a(multiplier_23_out), .b(multiplier_24_out), .out(adder_15_out));  // open: cin, cout
  Adder #(.width(16)) adder_16 (.a(multiplier_25_out), .b(multiplier_26_out), .out(adder_16_out));  // open: cin, cout
  Adder #(.width(16)) adder_17 (.a(multiplier_27_out), .b(multiplier_28_out), .out(adder_17_out));  // open: cin, cout
  Adder #(.width(16)) adder_18 (.a(multiplier_29_out), .b(multiplier_30_out), .out(adder_18_out));  // open: cin, cout
  Adder #(.width(16)) adder_19 (.a(multiplier_31_out), .b(multiplier_32_out), .out(adder_19_out));  // open: cin, cout
  Adder #(.width(16)) adder_20 (.a(multiplier_33_out), .b(multiplier_34_out), .out(adder_20_out));  // open: cin, cout
  Adder #(.width(16)) adder_21 (.a(multiplier_35_out), .b(multiplier_36_out), .out(adder_21_out));  // open: cin, cout
  Adder #(.width(16)) adder_22 (.a(multiplier_37_out), .b(multiplier_38_out), .out(adder_22_out));  // open: cin, cout
  Adder #(.width(16)) adder_23 (.a(multiplier_39_out), .b(multiplier_40_out), .out(adder_23_out));  // open: cin, cout
  Adder #(.width(16)) adder_24 (.a(adder_9_out), .b(adder_10_out), .out(C4));  // open: cin, cout
  Adder #(.width(16)) adder_25 (.a(multiplier_41_out), .b(multiplier_42_out), .out(adder_25_out));  // open: cin, cout
  Adder #(.width(16)) adder_26 (.a(multiplier_43_out), .b(multiplier_44_out), .out(adder_26_out));  // open: cin, cout
  Adder #(.width(16)) adder_27 (.a(multiplier_45_out), .b(multiplier_46_out), .out(adder_27_out));  // open: cin, cout
  Adder #(.width(16)) adder_28 (.a(multiplier_47_out), .b(multiplier_48_out), .out(adder_28_out));  // open: cin, cout
  Adder #(.width(16)) adder_29 (.a(multiplier_49_out), .b(multiplier_50_out), .out(adder_29_out));  // open: cin, cout
  Adder #(.width(16)) adder_30 (.a(multiplier_51_out), .b(multiplier_52_out), .out(adder_30_out));  // open: cin, cout
  Adder #(.width(16)) adder_31 (.a(adder_28_out), .b(adder_18_out), .out(C9));  // open: cin, cout
  Adder #(.width(16)) adder_32 (.a(adder_29_out), .b(adder_19_out), .out(C11));  // open: cin, cout
  Adder #(.width(16)) adder_33 (.a(adder_30_out), .b(adder_20_out), .out(C12));  // open: cin, cout
  Adder #(.width(16)) adder_34 (.a(adder_21_out), .b(adder_11_out), .out(C13));  // open: cin, cout
  Multiplier #(.width(16)) multiplier_53 (.a(A15), .b(B7), .out(multiplier_53_out));  // open: cin, cout
  Multiplier #(.width(16)) multiplier_54 (.a(A16), .b(B8), .out(multiplier_54_out));  // open: cin, cout
  Adder #(.width(16)) adder_35 (.a(adder_22_out), .b(adder_12_out), .out(C15));  // open: cin, cout
  Adder #(.width(16)) adder_36 (.a(adder_23_out), .b(adder_13_out), .out(C16));  // open: cin, cout
  Adder #(.width(16)) adder_37 (.a(adder_25_out), .b(adder_15_out), .out(C5));  // open: cin, cout
  Multiplier #(.width(16)) multiplier_55 (.a(A7), .b(B7), .out(multiplier_55_out));  // open: cin, cout
  Multiplier #(.width(16)) multiplier_56 (.a(A8), .b(B8), .out(multiplier_56_out));  // open: cin, cout
  Adder #(.width(16)) adder_38 (.a(adder_26_out), .b(adder_16_out), .out(C7));  // open: cin, cout
  Adder #(.width(16)) adder_39 (.a(adder_27_out), .b(adder_17_out), .out(C8));  // open: cin, cout
  Multiplier #(.width(16)) multiplier_57 (.a(A11), .b(B7), .out(multiplier_57_out));  // open: cin, cout
  Multiplier #(.width(16)) multiplier_58 (.a(A12), .b(B8), .out(multiplier_58_out));  // open: cin, cout
  Multiplier #(.width(16)) multiplier_59 (.a(A13), .b(B5), .out(multiplier_59_out));  // open: cin, cout
  Multiplier #(.width(16)) multiplier_60 (.a(A14), .b(B6), .out(multiplier_60_out));  // open: cin, cout
  Multiplier #(.width(16)) multiplier_61 (.a(A5), .b(B5), .out(multiplier_61_out));  // open: cin, cout
  Multiplier #(.width(16)) multiplier_62 (.a(A6), .b(B6), .out(multiplier_62_out));  // open: cin, cout
  Multiplier #(.width(16)) multiplier_63 (.a(A9), .b(B5), .out(multiplier_63_out));  // open: cin, cout
  Multiplier #(.width(16)) multiplier_64 (.a(A10), .b(B6), .out(multiplier_64_out));  // open: cin, cout
  Adder #(.width(16)) adder_40 (.a(multiplier_53_out), .b(multiplier_54_out), .out(adder_40_out));  // open: cin, cout
  Adder #(.width(16)) adder_41 (.a(multiplier_55_out), .b(multiplier_56_out), .out(adder_41_out));  // open: cin, cout
  Adder #(.width(16)) adder_42 (.a(multiplier_57_out), .b(multiplier_58_out), .out(adder_42_out));  // open: cin, cout
  Adder #(.width(16)) adder_43 (.a(multiplier_59_out), .b(multiplier_60_out), .out(adder_43_out));  // open: cin, cout
  Adder #(.width(16)) adder_44 (.a(multiplier_61_out), .b(multiplier_62_out), .out(adder_44_out));  // open: cin, cout
  Adder #(.width(16)) adder_45 (.a(multiplier_63_out), .b(multiplier_64_out), .out(adder_45_out));  // open: cin, cout
  Adder #(.width(16)) adder_46 (.a(adder_43_out), .b(adder_40_out), .out(C14));  // open: cin, cout
  Adder #(.width(16)) adder_47 (.a(adder_44_out), .b(adder_41_out), .out(C6));  // open: cin, cout
  Adder #(.width(16)) adder_48 (.a(adder_45_out), .b(adder_42_out), .out(C10));  // open: cin, cout
endmodule

module TilingAdder (
  input  [15:0] in_1,
  input  [15:0] in_2,
  input  [15:0] in_3,
  input  [15:0] in_4,
  input  [15:0] in_5,
  input  [15:0] in_6,
  input  [15:0] in_7,
  input  [15:0] in_8,
  input  [15:0] in_9,
  input  [15:0] in_10,
  input  [15:0] in_11,
  input  [15:0] in_12,
  input  [15:0] in_13,
  input  [15:0] in_14,
  input  [15:0] in_15,
  input  [15:0] in_16,
  input  [15:0] in_17,
  input  [15:0] in_18,
  input  [15:0] in_19,
  input  [15:0] in_20,
  input  [15:0] in_21,
  input  [15:0] in_22,
  input  [15:0] in_23,
  input  [15:0] in_24,
  input  [15:0] in_25,
  input  [15:0] in_26,
  input  [15:0] in_27,
  input  [15:0] in_28,
  input  [15:0] in_29,
  input  [15:0] in_30,
  input  [15:0] in_31,
  input  [15:0] in_32,
  output [15:0] out_33,
  output [15:0] out_34,
  output [15:0] out_35,
  output [15:0] out_36,
  output [15:0] out_37,
  output [15:0] out_38,
  output [15:0] out_39,
  output [15:0] out_40,
  output [15:0] out_41,
  output [15:0] out_42,
  output [15:0] out_43,
  output [15:0] out_44,
  output [15:0] out_45,
  output [15:0] out_46,
  output [15:0] out_47,
  output [15:0] out_48
);

  Adder #(.width(16)) adder_1 (.a(in_1), .b(in_2), .out(out_33));  // open: cin, cout
  Adder #(.width(16)) adder_2 (.a(in_3), .b(in_4), .out(out_34));  // open: cin, cout
  Adder #(.width(16)) adder_3 (.a(in_5), .b(in_6), .out(out_35));  // open: cin, cout
  Adder #(.width(16)) adder_4 (.a(in_7), .b(in_8), .out(out_36));  // open: cin, cout
  Adder #(.width(16)) adder_5 (.a(in_9), .b(in_10), .out(out_37));  // open: cin, cout
  Adder #(.width(16)) adder_6 (.a(in_11), .b(in_12), .out(out_38));  // open: cin, cout
  Adder #(.width(16)) adder_7 (.a(in_13), .b(in_14), .out(out_39));  // open: cin, cout
  Adder #(.width(16)) adder_8 (.a(in_15), .b(in_16), .out(out_40));  // open: cin, cout
  Adder #(.width(16)) adder_9 (.a(in_17), .b(in_18), .out(out_41));  // open: cin, cout
  Adder #(.width(16)) adder_10 (.a(in_19), .b(in_20), .out(out_42));  // open: cin, cout
  Adder #(.width(16)) adder_11 (.a(in_21), .b(in_22), .out(out_43));  // open: cin, cout
  Adder #(.width(16)) adder_12 (.a(in_23), .b(in_24), .out(out_44));  // open: cin, cout
  Adder #(.width(16)) adder_13 (.a(in_25), .b(in_26), .out(out_45));  // open: cin, cout
  Adder #(.width(16)) adder_14 (.a(in_27), .b(in_28), .out(out_46));  // open: cin, cout
  Adder #(.width(16)) adder_15 (.a(in_29), .b(in_30), .out(out_47));  // open: cin, cout
  Adder #(.width(16)) adder_16 (.a(in_31), .b(in_32), .out(out_48));  // open: cin, cout
endmodule

module TILINGwINSTPrototype1 (
  input  in_1,
  input  in_2,
  input  in_3
);

  wire clock_1_out, comparator_1_eq, comparator_2_eq, comparator_4_eq, comparator_5_eq, comparator_6_eq,
       counter_2_q, counter_5_q, counter_8_q, or_1_out, or_2_out, or_3_out, or_4_out, or_5_out, or_6_out,
       or_7_out, or_8_out, register_1_q, register_2_q, register_6_q, undriven, undriven_2, xor_1_out;
  wire [3:0] counter_3_q, counter_4_q, counter_6_q, multiplier_1_out, register_4_q, subtractor_1_out;
  wire [7:0] counter_1_q, counter_7_q, counter_9_q, counter_10_q, counter_11_q;
  wire [7:4] register_5_q;
  wire [15:0] adder_1_out, adder_2_out, adder_3_out, adder_4_out, adder_5_out, adder_6_out, adder_7_out,
       adder_8_out, adder_9_out, adder_10_out, adder_11_out, adder_12_out, adder_13_out, adder_14_out,
       adder_15_out, adder_16_out, controlled_buffer_1_out, ram_1_dout, ram_2_dout, ram_3_dout, register_3_q,
       register_7_q, register_8_q, register_9_q, register_10_q, register_11_q, register_12_q, register_13_q,
       register_14_q, register_15_q, register_16_q, register_17_q, register_18_q, register_19_q,
       register_20_q, register_21_q, register_22_q, register_23_q, register_24_q, register_25_q,
       register_26_q, register_27_q, register_28_q, register_29_q, register_30_q, register_31_q,
       register_32_q, register_33_q, register_34_q, register_35_q, register_36_q, register_37_q,
       register_38_q, register_39_q, register_40_q, register_41_q, register_42_q, register_43_q,
       register_44_q, register_45_q, register_46_q, register_47_q, register_48_q, register_49_q,
       register_50_q, register_51_q, register_52_q, register_53_q, register_54_q, tilingcore_1_c1,
       tilingcore_1_c2, tilingcore_1_c3, tilingcore_1_c4, tilingcore_1_c5, tilingcore_1_c6, tilingcore_1_c7,
       tilingcore_1_c8, tilingcore_1_c9, tilingcore_1_c10, tilingcore_1_c11, tilingcore_1_c12,
       tilingcore_1_c13, tilingcore_1_c14, tilingcore_1_c15, tilingcore_1_c16;
  wire [63:0] rom_1_data;

  Clock clock_1 (.out(clock_1_out));
  xor xor_1 (xor_1_out, rom_1_data[0], comparator_2_eq);
  or or_1 (or_1_out, xor_1_out, rom_1_data[2]);
  Counter counter_1 (.count(or_2_out), .Q(counter_1_q), .clk(clock_1_out));  // open: load, D, carry, up, clr
  Counter #(.max('h1), .width(1)) counter_2 (
    .load(rom_1_data[0]), .D(rom_1_data[0]), .count(rom_1_data[0]), .Q(counter_2_q), .clk(clock_1_out));  // open: carry, up, clr
  // Probe on counter_3_q
  Counter #(.max('hf), .width(4)) counter_3 (
    .Q(counter_3_q), .clk(clock_1_out), .clr(register_1_q));  // open: load, D, count, carry, up
  Register #(.width(1)) register_1 (
    .D(or_1_out), .en(or_1_out), .clk(clock_1_out), .Q(register_1_q), .clr(register_1_q));
  RAM #(.dataWidth(16), .\type ("nonvolatile")) ram_1 (
    .addr(counter_1_q), .oe(or_2_out), .clk(clock_1_out), .dout(ram_1_dout));  // open: we, din
  or or_2 (or_2_out, comparator_1_eq, rom_1_data[1]);
  Comparator #(.width(1)) comparator_1 (.a(in_3), .b(counter_2_q), .eq(comparator_1_eq));  // open: gt, lt
  // Probe on register_5_q
  Comparator #(.width(4)) comparator_2 (.a(counter_4_q), .b(counter_3_q), .eq(comparator_2_eq));  // open: gt, lt
  Register #(.width(1)) register_2 (
    .D(undriven), .en(undriven), .clk(undriven_2), .Q(register_2_q), .clr(register_2_q));
  ROM #(.dataWidth(64)) rom_1 (.addr({register_5_q, counter_3_q}), .data(rom_1_data));
  // Probe on ram_1_dout
  Register #(.width(16)) register_3 (
    .D(ram_1_dout), .en(rom_1_data[1]), .clk(clock_1_out), .Q(register_3_q));  // open: clr
  Multiplier #(.width(4)) multiplier_1 (.a(register_4_q), .b(4'b0100), .out(multiplier_1_out));  // open: cin, cout
  Subtractor #(.width(4)) subtractor_1 (.a(multiplier_1_out), .b(4'b0001), .out(subtractor_1_out));  // open: bin, bout
  Counter #(.max('hf), .width(4)) counter_4 (
    .load(1'b1), .D(subtractor_1_out), .Q(counter_4_q), .clk(clock_1_out), .clr(register_6_q));  // open: count, carry, up
  or or_3 (or_3_out, xor_1_out, rom_1_data[3]);
  Register #(.width(4)) register_4 (
    .D(register_3_q[3:0]), .en(rom_1_data[5]), .clk(clock_1_out), .Q(register_4_q), .clr(register_6_q));
  Register #(.width(4)) register_5 (
    .D(register_3_q[15:12]), .en(rom_1_data[7]), .clk(clock_1_out), .Q(register_5_q), .clr(register_6_q));
  Register #(.width(1)) register_6 (
    .D(or_3_out), .en(or_3_out), .clk(clock_1_out), .Q(register_6_q), .clr(register_6_q));
  Counter #(.max('h1), .width(1)) counter_5 (
    .load(rom_1_data[0]), .D(rom_1_data[0]), .count(rom_1_data[0]), .Q(counter_5_q), .clk(clock_1_out));  // open: carry, up, clr
  Comparator #(.width(4)) comparator_3 (.a(4'b0101), .b(counter_6_q));  // open: gt, eq, lt
  Counter #(.max('hf), .width(4)) counter_6 (
    .Q(counter_6_q), .clk(rom_1_data[4]));  // open: load, D, count, carry, up, clr
  Comparator #(.width(1)) comparator_4 (.a(in_2), .b(counter_5_q), .eq(comparator_4_eq));  // open: gt, lt
  Counter counter_7 (
    .load(rom_1_data[6]), .D(register_3_q[11:4]), .count(or_4_out), .Q(counter_7_q), .clk(clock_1_out),
    .clr(register_6_q));  // open: carry, up
  or or_4 (or_4_out, comparator_4_eq, or_5_out);
  RAM #(.dataWidth(16), .\type ("nonvolatile")) ram_2 (
    .addr(counter_7_q), .oe(or_4_out), .clk(clock_1_out), .dout(ram_2_dout));  // open: we, din
  or or_5 (or_5_out, rom_1_data[23], rom_1_data[22], rom_1_data[21], rom_1_data[20], rom_1_data[19], rom_1_data[18], rom_1_data[17], rom_1_data[16], rom_1_data[15], rom_1_data[14], rom_1_data[13], rom_1_data[12], rom_1_data[11], rom_1_data[10], rom_1_data[9], rom_1_data[8]);
  Register #(.width(16)) register_7 (
    .D(ram_2_dout), .en(rom_1_data[8]), .clk(clock_1_out), .Q(register_7_q), .clr(1'b0));
  Register #(.width(16)) register_8 (
    .D(ram_2_dout), .en(rom_1_data[9]), .clk(clock_1_out), .Q(register_8_q), .clr(1'b0));
  Register #(.width(16)) register_9 (
    .D(ram_2_dout), .en(rom_1_data[10]), .clk(clock_1_out), .Q(register_9_q), .clr(1'b0));
  Register #(.width(16)) register_10 (
    .D(ram_2_dout), .en(rom_1_data[11]), .clk(clock_1_out), .Q(register_10_q), .clr(1'b0));
  Register #(.width(16)) register_11 (
    .D(ram_2_dout), .en(rom_1_data[12]), .clk(clock_1_out), .Q(register_11_q), .clr(1'b0));
  Register #(.width(16)) register_12 (
    .D(ram_2_dout), .en(rom_1_data[13]), .clk(clock_1_out), .Q(register_12_q), .clr(1'b0));
  Register #(.width(16)) register_13 (
    .D(ram_2_dout), .en(rom_1_data[14]), .clk(clock_1_out), .Q(register_13_q), .clr(1'b0));
  Register #(.width(16)) register_14 (
    .D(ram_2_dout), .en(rom_1_data[15]), .clk(clock_1_out), .Q(register_14_q), .clr(1'b0));
  Register #(.width(16)) register_15 (
    .D(ram_2_dout), .en(rom_1_data[16]), .clk(clock_1_out), .Q(register_15_q), .clr(1'b0));
  Register #(.width(16)) register_16 (
    .D(ram_2_dout), .en(rom_1_data[17]), .clk(clock_1_out), .Q(register_16_q), .clr(1'b0));
  Register #(.width(16)) register_17 (
    .D(ram_2_dout), .en(rom_1_data[18]), .clk(clock_1_out), .Q(register_17_q), .clr(1'b0));
  Register #(.width(16)) register_18 (
    .D(ram_2_dout), .en(rom_1_data[19]), .clk(clock_1_out), .Q(register_18_q), .clr(1'b0));
  Register #(.width(16)) register_19 (
    .D(ram_2_dout), .en(rom_1_data[20]), .clk(clock_1_out), .Q(register_19_q), .clr(1'b0));
  Register #(.width(16)) register_20 (
    .D(ram_2_dout), .en(rom_1_data[21]), .clk(clock_1_out), .Q(register_20_q), .clr(1'b0));
  Register #(.width(16)) register_21 (
    .D(ram_2_dout), .en(rom_1_data[22]), .clk(clock_1_out), .Q(register_21_q), .clr(1'b0));
  Register #(.width(16)) register_22 (
    .D(ram_2_dout), .en(rom_1_data[23]), .clk(clock_1_out), .Q(register_22_q), .clr(1'b0));
  Counter #(.max('h1), .width(1)) counter_8 (
    .load(rom_1_data[0]), .D(rom_1_data[0]), .count(rom_1_data[0]), .Q(counter_8_q), .clk(clock_1_out));  // open: carry, up, clr
  Comparator #(.width(1)) comparator_5 (.a(in_1), .b(counter_8_q), .eq(comparator_5_eq));  // open: gt, lt
  or or_6 (or_6_out, comparator_5_eq, or_7_out);
  RAM #(.dataWidth(16), .\type ("nonvolatile")) ram_3 (
    .addr(counter_9_q), .oe(or_6_out), .clk(clock_1_out), .dout(ram_3_dout));  // open: we, din
  Counter counter_9 (
    .load(rom_1_data[6]), .D(register_3_q[11:4]), .count(or_6_out), .Q(counter_9_q), .clk(clock_1_out));  // open: carry, up, clr
  or or_7 (or_7_out, rom_1_data[39], rom_1_data[38], rom_1_data[37], rom_1_data[36], rom_1_data[35], rom_1_data[34], rom_1_data[33], rom_1_data[32], rom_1_data[31], rom_1_data[30], rom_1_data[29], rom_1_data[28], rom_1_data[27], rom_1_data[26], rom_1_data[25], rom_1_data[24]);
  Register #(.width(16)) register_23 (
    .D(ram_3_dout), .en(rom_1_data[24]), .clk(clock_1_out), .Q(register_23_q), .clr(1'b0));
  Register #(.width(16)) register_24 (
    .D(ram_3_dout), .en(rom_1_data[25]), .clk(clock_1_out), .Q(register_24_q), .clr(1'b0));
  Register #(.width(16)) register_25 (
    .D(ram_3_dout), .en(rom_1_data[26]), .clk(clock_1_out), .Q(register_25_q), .clr(1'b0));
  Register #(.width(16)) register_26 (
    .D(ram_3_dout), .en(rom_1_data[27]), .clk(clock_1_out), .Q(register_26_q), .clr(1'b0));
  Register #(.width(16)) register_27 (
    .D(ram_3_dout), .en(rom_1_data[28]), .clk(clock_1_out), .Q(register_27_q), .clr(1'b0));
  Register #(.width(16)) register_28 (
    .D(ram_3_dout), .en(rom_1_data[29]), .clk(clock_1_out), .Q(register_28_q), .clr(1'b0));
  Register #(.width(16)) register_29 (
    .D(ram_3_dout), .en(rom_1_data[30]), .clk(clock_1_out), .Q(register_29_q), .clr(1'b0));
  Register #(.width(16)) register_30 (
    .D(ram_3_dout), .en(rom_1_data[31]), .clk(clock_1_out), .Q(register_30_q), .clr(1'b0));
  Register #(.width(16)) register_31 (
    .D(ram_3_dout), .en(rom_1_data[32]), .clk(clock_1_out), .Q(register_31_q), .clr(1'b0));
  Register #(.width(16)) register_32 (
    .D(ram_3_dout), .en(rom_1_data[33]), .clk(clock_1_out), .Q(register_32_q), .clr(1'b0));
  Register #(.width(16)) register_33 (
    .D(ram_3_dout), .en(rom_1_data[34]), .clk(clock_1_out), .Q(register_33_q), .clr(1'b0));
  Register #(.width(16)) register_34 (
    .D(ram_3_dout), .en(rom_1_data[35]), .clk(clock_1_out), .Q(register_34_q), .clr(1'b0));
  Register #(.width(16)) register_35 (
    .D(ram_3_dout), .en(rom_1_data[36]), .clk(clock_1_out), .Q(register_35_q), .clr(1'b0));
  Register #(.width(16)) register_36 (
    .D(ram_3_dout), .en(rom_1_data[37]), .clk(clock_1_out), .Q(register_36_q), .clr(1'b0));
  Register #(.width(16)) register_37 (
    .D(ram_3_dout), .en(rom_1_data[38]), .clk(clock_1_out), .Q(register_37_q), .clr(1'b0));
  Register #(.width(16)) register_38 (
    .D(ram_3_dout), .en(rom_1_data[39]), .clk(clock_1_out), .Q(register_38_q), .clr(1'b0));
  TilingCore tilingcore_1 (
    .A1(register_7_q), .A2(register_8_q), .A3(register_9_q), .A4(register_10_q), .B1(register_23_q),
    .B2(register_24_q), .B3(register_25_q), .B4(register_26_q), .A5(register_11_q), .A6(register_12_q),
    .A7(register_13_q), .A8(register_14_q), .B5(register_27_q), .B6(register_28_q), .B7(register_29_q),
    .B8(register_30_q), .A9(register_15_q), .A10(register_16_q), .A11(register_17_q), .A12(register_18_q),
    .B9(register_31_q), .B10(register_32_q), .B11(register_33_q), .B12(register_34_q), .A13(register_19_q),
    .A14(register_20_q), .A15(register_21_q), .A16(register_22_q), .B13(register_35_q), .B14(register_36_q),
    .B15(register_37_q), .B16(register_38_q), .C1(tilingcore_1_c1), .C2(tilingcore_1_c2),
    .C3(tilingcore_1_c3), .C4(tilingcore_1_c4), .C5(tilingcore_1_c5), .C6(tilingcore_1_c6),
    .C7(tilingcore_1_c7), .C8(tilingcore_1_c8), .C9(tilingcore_1_c9), .C10(tilingcore_1_c10),
    .C11(tilingcore_1_c11), .C12(tilingcore_1_c12), .C13(tilingcore_1_c13), .C14(tilingcore_1_c14),
    .C15(tilingcore_1_c15), .C16(tilingcore_1_c16));
  Counter #(.trigger("falling")) counter_10 (
    .Q(counter_10_q), .clk(rom_1_data[63]), .clr(comparator_6_eq));  // open: load, D, count, carry, up
  Comparator comparator_6 (.a(8'h1), .b(counter_10_q), .eq(comparator_6_eq));  // open: gt, lt
  Adder #(.width(16)) adder_1 (.a(register_39_q), .b(tilingcore_1_c1), .out(adder_1_out));  // open: cin, cout
  Adder #(.width(16)) adder_2 (.a(register_40_q), .b(tilingcore_1_c2), .out(adder_2_out));  // open: cin, cout
  Adder #(.width(16)) adder_3 (.a(register_41_q), .b(tilingcore_1_c3), .out(adder_3_out));  // open: cin, cout
  Adder #(.width(16)) adder_4 (.a(register_42_q), .b(tilingcore_1_c4), .out(adder_4_out));  // open: cin, cout
  Adder #(.width(16)) adder_5 (.a(register_43_q), .b(tilingcore_1_c5), .out(adder_5_out));  // open: cin, cout
  Adder #(.width(16)) adder_6 (.a(register_44_q), .b(tilingcore_1_c6), .out(adder_6_out));  // open: cin, cout
  Adder #(.width(16)) adder_7 (.a(register_45_q), .b(tilingcore_1_c7), .out(adder_7_out));  // open: cin, cout
  Adder #(.width(16)) adder_8 (.a(register_46_q), .b(tilingcore_1_c8), .out(adder_8_out));  // open: cin, cout
  Adder #(.width(16)) adder_9 (.a(register_47_q), .b(tilingcore_1_c9), .out(adder_9_out));  // open: cin, cout
  Adder #(.width(16)) adder_10 (.a(register_48_q), .b(tilingcore_1_c10), .out(adder_10_out));  // open: cin, cout
  Adder #(.width(16)) adder_11 (.a(register_49_q), .b(tilingcore_1_c11), .out(adder_11_out));  // open: cin, cout
  Adder #(.width(16)) adder_12 (.a(register_50_q), .b(tilingcore_1_c12), .out(adder_12_out));  // open: cin, cout
  Adder #(.width(16)) adder_13 (.a(register_51_q), .b(tilingcore_1_c13), .out(adder_13_out));  // open: cin, cout
  Adder #(.width(16)) adder_14 (.a(register_52_q), .b(tilingcore_1_c14), .out(adder_14_out));  // open: cin, cout
  Adder #(.width(16)) adder_15 (.a(register_53_q), .b(tilingcore_1_c15), .out(adder_15_out));  // open: cin, cout
  Adder #(.width(16)) adder_16 (.a(register_54_q), .b(tilingcore_1_c16), .out(adder_16_out));  // open: cin, cout
  Register #(.width(16)) register_39 (
    .D(adder_1_out), .en(rom_1_data[47]), .clk(clock_1_out), .Q(register_39_q), .clr(comparator_6_eq));
  Register #(.width(16)) register_40 (
    .D(adder_2_out), .en(rom_1_data[47]), .clk(clock_1_out), .Q(register_40_q), .clr(comparator_6_eq));
  Register #(.width(16)) register_41 (
    .D(adder_3_out), .en(rom_1_data[47]), .clk(clock_1_out), .Q(register_41_q), .clr(comparator_6_eq));
  Register #(.width(16)) register_42 (
    .D(adder_4_out), .en(rom_1_data[47]), .clk(clock_1_out), .Q(register_42_q), .clr(comparator_6_eq));
  Register #(.width(16)) register_43 (
    .D(adder_5_out), .en(rom_1_data[47]), .clk(clock_1_out), .Q(register_43_q), .clr(comparator_6_eq));
  Register #(.width(16)) register_44 (
    .D(adder_6_out), .en(rom_1_data[47]), .clk(clock_1_out), .Q(register_44_q), .clr(comparator_6_eq));
  Register #(.width(16)) register_45 (
    .D(adder_7_out), .en(rom_1_data[47]), .clk(clock_1_out), .Q(register_45_q), .clr(comparator_6_eq));
  Register #(.width(16)) register_46 (
    .D(adder_8_out), .en(rom_1_data[47]), .clk(clock_1_out), .Q(register_46_q), .clr(comparator_6_eq));
  Register #(.width(16)) register_47 (
    .D(adder_9_out), .en(rom_1_data[47]), .clk(clock_1_out), .Q(register_47_q), .clr(comparator_6_eq));
  Register #(.width(16)) register_48 (
    .D(adder_10_out), .en(rom_1_data[47]), .clk(clock_1_out), .Q(register_48_q), .clr(comparator_6_eq));
  Register #(.width(16)) register_49 (
    .D(adder_11_out), .en(rom_1_data[47]), .clk(clock_1_out), .Q(register_49_q), .clr(comparator_6_eq));
  Register #(.width(16)) register_50 (
    .D(adder_12_out), .en(rom_1_data[47]), .clk(clock_1_out), .Q(register_50_q), .clr(comparator_6_eq));
  Register #(.width(16)) register_51 (
    .D(adder_13_out), .en(rom_1_data[47]), .clk(clock_1_out), .Q(register_51_q), .clr(comparator_6_eq));
  Register #(.width(16)) register_52 (
    .D(adder_14_out), .en(rom_1_data[47]), .clk(clock_1_out), .Q(register_52_q), .clr(comparator_6_eq));
  Register #(.width(16)) register_53 (
    .D(adder_15_out), .en(rom_1_data[47]), .clk(clock_1_out), .Q(register_53_q), .clr(comparator_6_eq));
  Register #(.width(16)) register_54 (
    .D(adder_16_out), .en(rom_1_data[47]), .clk(clock_1_out), .Q(register_54_q), .clr(comparator_6_eq));
  assign controlled_buffer_1_out = rom_1_data[48] ? register_39_q : 16'bz;  // Controlled_Buffer controlled_buffer_1
  assign controlled_buffer_1_out = rom_1_data[49] ? register_40_q : 16'bz;  // Controlled_Buffer controlled_buffer_2
  assign controlled_buffer_1_out = rom_1_data[50] ? register_41_q : 16'bz;  // Controlled_Buffer controlled_buffer_3
  assign controlled_buffer_1_out = rom_1_data[51] ? register_42_q : 16'bz;  // Controlled_Buffer controlled_buffer_4
  assign controlled_buffer_1_out = rom_1_data[52] ? register_43_q : 16'bz;  // Controlled_Buffer controlled_buffer_5
  assign controlled_buffer_1_out = rom_1_data[53] ? register_44_q : 16'bz;  // Controlled_Buffer controlled_buffer_6
  assign controlled_buffer_1_out = rom_1_data[54] ? register_45_q : 16'bz;  // Controlled_Buffer controlled_buffer_7
  assign controlled_buffer_1_out = rom_1_data[55] ? register_46_q : 16'bz;  // Controlled_Buffer controlled_buffer_8
  assign controlled_buffer_1_out = rom_1_data[56] ? register_47_q : 16'bz;  // Controlled_Buffer controlled_buffer_9
  assign controlled_buffer_1_out = rom_1_data[57] ? register_48_q : 16'bz;  // Controlled_Buffer controlled_buffer_10
  assign controlled_buffer_1_out = rom_1_data[58] ? register_49_q : 16'bz;  // Controlled_Buffer controlled_buffer_11
  assign controlled_buffer_1_out = rom_1_data[59] ? register_50_q : 16'bz;  // Controlled_Buffer controlled_buffer_12
  assign controlled_buffer_1_out = rom_1_data[60] ? register_51_q : 16'bz;  // Controlled_Buffer controlled_buffer_13
  assign controlled_buffer_1_out = rom_1_data[61] ? register_52_q : 16'bz;  // Controlled_Buffer controlled_buffer_14
  assign controlled_buffer_1_out = rom_1_data[62] ? register_53_q : 16'bz;  // Controlled_Buffer controlled_buffer_15
  assign controlled_buffer_1_out = rom_1_data[63] ? register_54_q : 16'bz;  // Controlled_Buffer controlled_buffer_16
  or or_8 (or_8_out, rom_1_data[48], rom_1_data[49], rom_1_data[50], rom_1_data[51], rom_1_data[52], rom_1_data[53], rom_1_data[54], rom_1_data[55], rom_1_data[56], rom_1_data[57], rom_1_data[58], rom_1_data[59], rom_1_data[60], rom_1_data[61], rom_1_data[62], rom_1_data[63]);
  Counter counter_11 (.count(or_8_out), .Q(counter_11_q), .clk(clock_1_out));  // open: load, D, carry, up, clr
  RAM #(.dataWidth(16)) ram_4 (
    .addr(counter_11_q), .we(or_8_out), .clk(clock_1_out), .din(controlled_buffer_1_out));  // open: oe, dout
  RAM #(.dataWidth(16), .\type ("nonvolatile")) ram_5 ();  // open: addr, we, oe, clk, din, dout
  RAM #(.dataWidth(16), .\type ("nonvolatile")) ram_6 ();  // open: addr, we, oe, clk, din, dout
  RAM #(.dataWidth(16), .\type ("nonvolatile")) ram_7 ();  // open: addr, we, oe, clk, din, dout
  RAM #(.dataWidth(16), .\type ("nonvolatile")) ram_8 ();  // open: addr, we, oe, clk, din, dout

  // Notes on the sheet:
  //   1. INST RAM
  //   1. MBR
  //   1. RES ROM Count
  //   2. Flag
  //   2. DIM
  //   2. Add
  //   2. OPC
  //   Used OR Gate Bcoz
  //   COMP with dim will
  //    reset PCU
  //   and JMP
  //   statement also req
  //   PCU Reset
  //   PC
  //   ROM COUNTER
  //   JMP + RESET
  //   RESETS PCU (DOESNT
  //   RESET OPC SIGNAL)
  //   RAM GARBAGE CONTROLLER
  //   ONLY CLEAR GARBAGE WHEN
  //   CYCLE = 1
  //   USED XOR GATE TO NULLIFY FIRST == SIGNAL FROM COMPARATOR
  //   OPCODE
  //   DECODER
  //   THIS WILL ALSO GET RESET WITH OPC ONCE
  //   DIMENSION = COUNT
  //   DIMENSION SHOULD ONLY BE INCLUDED IN LOAD A AND B
  //   ADDRESS OF FIRST MATRIX SHOULD BE +1 BCOZ OF GARBAGE
  //   ADDRESS SHOULD BE INCLUDED IN LOAD A, B AND STORE C
  //   INSTRUCTION RAM
  //   contents of rom_1 (hex, n*v repeats v):
  //   1 2 f4 13*0 100 200 400 800 1000 2000 4000 8000 10000 20000 40000 80000 100000 200000 400000 800008
  //   1000000 2000000 4000000 8000000 10000000 20000000 40000000 80000000 100000000 200000000 400000000
  //   800000000 1000000000 2000000000 4000000000 8000000008 800000000000 15*0 1000000000000 2000000000000
  //   4000000000000 8000000000000 10000000000000 20000000000000 40000000000000 80000000000000
  //   100000000000000 200000000000000 400000000000000 800000000000000 1000000000000000 2000000000000000
  //   4000000000000000 8000000000000000 1c
  //   PULSE GENERATOR
  //   ROM PCU
  //   MBR
  //   RESET SYNC
  //   RESET OPC SIGNAL
  //   THIS WILL ALSO GET RESET WITH OPC ONCE
  //   RESET LINE FOR ALL REGISTER, RESET WHEN OPCC LOADS VALUE 4 TIMES
  //   ADDRESS IS DIRECTLY CONNECTED TO COUNTER WE
  //   ADD PADDING MANUALLY FOR Less < 4x4 Matrices
  //   RESULTANT MATRIX IS TRANSPOSED
endmodule
